# Fritzing sketch AlarmClock (saved by Fritzing 1.0.8)

parts:
  A1 = Raspberry Pi 5
  Part1 = SPI OLED Monochrome 128x64 0.96 inch
  Part2 = 24 NeoPixel Ring [part_number=1586]
  Part3 = 16 NeoPixel Ring [part_number=1463]

nets:
  VDD: A1.5V, Part2.VDD, Part3.VDD
  GND: A1.GND, Part1.GND, Part2.GND, Part3.GND
  3V3: A1.3V3, Part1.VDD
  N1: A1.GPIO24, Part1.DC
  N2: A1.GPIO10, Part1.SDA
  N3: A1.GPIO25, Part1.RES
  N4: A1.GPIO11, Part1.SCK
  N5: A1.GPIO8, Part1.CS
  N6: A1.GPIO20, Part2.IN
  N7: Part2.OUT, Part3.IN

custom parts:
  Raspberry Pi 5: The RPi5, a faster version of the awesome Raspberry Pi4B ARM Board with 40 pin gpio.
  SPI OLED Monochrome 128x64 0.96 inch: Unknown 128x64 0.96 inch 128x64 SPI Monochrome OLED display
  24 NeoPixel Ring: 24 ultra bright smart LED NeoPixels are arranged in a circle with 2.6" (66mm) outer diameter. The rings are 'chainable' - connect the output pin of one to the input pin of another. Use only one microcontroller pin to control as many as you can chain together! Each LED is addressable as the driver chip is inside the LED. Each one has ~18mA constant current drive so the color will be very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
  16 NeoPixel Ring: 16 ultra bright smart LED NeoPixels are arranged in a circle with 1.75" (44.5mm) outer diameter. The rings are 'chainable' - connect the output pin of one to the input pin of another. Use only one microcontroller pin to control as many as you can chain together! Each LED is addressable as the driver chip is inside the LED. Each one has ~18mA constant current drive so the color will be very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
